// Logisim project hw4.circ as structural Verilog: 15 circuits, main circuit main
module main (
  input  sub,
  input  WE,
  input  reset,
  input  [2:0] ALUop,
  input  Rdst,
  input  [2:0] rd,
  input  [2:0] rs,
  input  [2:0] rt,
  input  [5:0] imm,
  input  ALUinB
);

  wire _0, _1, _2, _3, _4, _5, _6, _7, _8, _9, _10, _11, _12, _13, _14, _15, clock_out;
  wire [2:0] multiplexer_1_out;
  wire [15:0] addermain_1_result, alu_1_outputdata, bit_extender_1_out, multiplexer_2_out, register_1_output,
       registerfile_1_rs2val, registerfile_1_rs_nval;

  addermain addermain_1 (.result(addermain_1_result), .sub(1'b0), .A(register_1_output), .B(16'h1));  // open: ovf
  register register_1 (.\input (addermain_1_result), .\output (register_1_output));  // open: clock, reset, WE
  control control_1 (.opcode({_12, _13, _14, _15}));  // open: BR, JP, DMwe, Rwe
  ROM #(.addrWidth(16), .dataWidth(16)) rom_1 (
    .addr(register_1_output), .data({_15, _14, _13, _12, _11, _10, _9, _8, _7, _6, _5, _4, _3, _2, _1, _0}));  // open: sel
  Clock #(.highDuration(10)) clock (.out(clock_out));
  Multiplexer #(.width(3), .enable("false")) multiplexer_1 (.in0(rd), .in1(rt), .out(multiplexer_1_out), .sel(Rdst));
  RegisterFile registerfile_1 (
    .RDVAL(alu_1_outputdata), .RS_nVAL(registerfile_1_rs_nval), .RS2VAL(registerfile_1_rs2val),
    .clock(clock_out), .WE(WE), .RD(multiplexer_1_out), .reset(reset), .RS1(rs), .RS2(rt));
  Multiplexer #(.width(16), .enable("false")) multiplexer_2 (
    .in0(registerfile_1_rs2val), .in1(bit_extender_1_out), .out(multiplexer_2_out), .sel(ALUinB));
  assign bit_extender_1_out = {{10{imm[5]}}, imm};  // Bit_Extender bit_extender_1
  ALU alu_1 (
    .sub(sub), .InputData1(registerfile_1_rs_nval), .InputData2(multiplexer_2_out), .shamt({_0, _1, _2}),
    .OpType(ALUop), .OutputData(alu_1_outputdata));  // open: z
  TTY #(.rows(13), .cols(80), .trigger("falling")) tty_1 ();  // open: data, clk, we, clr
  RAM #(.addrWidth(16), .dataWidth(16)) ram_1 ();  // open: addr, data, sel, clk, ld, clr

  // Other names for the same wires on the sheet: opcode[3:0] = {_12, _13, _14, _15};
  //   address[11:0] = {_0, _1, _2, _3, _4, _5, _6, _7, _8, _9, _10, _11}; rs_t[2:0] = {_9, _10, _11};
  //   rt_t[2:0] = {_7, _8, _9}; rd_t[2:0] = {_6, _7, _8}; imm_t[5:0] = {_0, _1, _2, _3, _4, _5};
  //   shamt[2:0] = {_0, _1, _2}

  // Notes on the sheet:
  //   1 for itype
  //   purposelly disconnected
endmodule

module register (
  input  clock,
  input  reset,
  input  WE,
  input  [15:0] \input ,
  output [15:0] \output 
);

  D_Flip_Flop d_ff_1 (.clk(clock), .D(\input [0]), .Q(\output [0]), .en(WE), .reset(reset));  // open: Qn, preset
  D_Flip_Flop d_ff_2 (.clk(clock), .D(\input [1]), .Q(\output [1]), .en(WE), .reset(reset));  // open: Qn, preset
  D_Flip_Flop d_ff_3 (.clk(clock), .D(\input [2]), .Q(\output [2]), .en(WE), .reset(reset));  // open: Qn, preset
  D_Flip_Flop d_ff_4 (.clk(clock), .D(\input [3]), .Q(\output [3]), .en(WE), .reset(reset));  // open: Qn, preset
  D_Flip_Flop d_ff_5 (.clk(clock), .D(\input [4]), .Q(\output [4]), .en(WE), .reset(reset));  // open: Qn, preset
  D_Flip_Flop d_ff_6 (.clk(clock), .D(\input [5]), .Q(\output [5]), .en(WE), .reset(reset));  // open: Qn, preset
  D_Flip_Flop d_ff_7 (.clk(clock), .D(\input [6]), .Q(\output [6]), .en(WE), .reset(reset));  // open: Qn, preset
  D_Flip_Flop d_ff_8 (.clk(clock), .D(\input [7]), .Q(\output [7]), .en(WE), .reset(reset));  // open: Qn, preset
  D_Flip_Flop d_ff_9 (.clk(clock), .D(\input [8]), .Q(\output [8]), .en(WE), .reset(reset));  // open: Qn, preset
  D_Flip_Flop d_ff_10 (.clk(clock), .D(\input [9]), .Q(\output [9]), .en(WE), .reset(reset));  // open: Qn, preset
  D_Flip_Flop d_ff_11 (.clk(clock), .D(\input [10]), .Q(\output [10]), .en(WE), .reset(reset));  // open: Qn, preset
  D_Flip_Flop d_ff_12 (.clk(clock), .D(\input [11]), .Q(\output [11]), .en(WE), .reset(reset));  // open: Qn, preset
  D_Flip_Flop d_ff_13 (.clk(clock), .D(\input [12]), .Q(\output [12]), .en(WE), .reset(reset));  // open: Qn, preset
  D_Flip_Flop d_ff_14 (.clk(clock), .D(\input [13]), .Q(\output [13]), .en(WE), .reset(reset));  // open: Qn, preset
  D_Flip_Flop d_ff_15 (.clk(clock), .D(\input [14]), .Q(\output [14]), .en(WE), .reset(reset));  // open: Qn, preset
  D_Flip_Flop d_ff_16 (.clk(clock), .D(\input [15]), .Q(\output [15]), .en(WE), .reset(reset));  // open: Qn, preset

  // Other names for the same wires on the sheet: clear = reset
endmodule

module RegisterFile (
  input  [15:0] RDVAL,
  input  clock,
  input  WE,
  input  [2:0] RD,
  input  reset,
  input  [2:0] RS1,
  input  [2:0] RS2,
  output [15:0] RS_nVAL,
  output [15:0] RS2VAL
);

  wire and_1_out, and_2_out, and_3_out, and_4_out, and_5_out, and_6_out, and_7_out, and_8_out,
       decoder_1_out0, decoder_1_out1, decoder_1_out2, decoder_1_out3, decoder_1_out4, decoder_1_out5,
       decoder_1_out6, decoder_1_out7, decoder_2_out0, decoder_2_out1, decoder_2_out2, decoder_2_out3,
       decoder_2_out4, decoder_2_out5, decoder_2_out6, decoder_2_out7, decoder_3_out0, decoder_3_out1,
       decoder_3_out2, decoder_3_out3, decoder_3_out4, decoder_3_out5, decoder_3_out6, decoder_3_out7;
  wire [15:0] register_1_output, register_2_output, register_3_output, register_4_output, register_5_output,
       register_6_output, register_7_output, register_8_output;

  // Probe on and_1_out
  // Probe on and_2_out
  and and_1 (and_1_out, WE, decoder_1_out0);
  register register_1 (.clock(clock), .reset(reset), .WE(and_1_out), .\input (RDVAL), .\output (register_1_output));
  and and_2 (and_2_out, WE, decoder_1_out1);
  register register_2 (.clock(clock), .reset(reset), .WE(and_2_out), .\input (RDVAL), .\output (register_2_output));
  // Probe on and_3_out
  and and_3 (and_3_out, WE, decoder_1_out2);
  register register_3 (.clock(clock), .reset(reset), .WE(and_3_out), .\input (RDVAL), .\output (register_3_output));
  Decoder #(.select(3), .enable("false")) decoder_1 (
    .out0(decoder_1_out0), .out1(decoder_1_out1), .out2(decoder_1_out2), .out3(decoder_1_out3),
    .out4(decoder_1_out4), .out5(decoder_1_out5), .out6(decoder_1_out6), .out7(decoder_1_out7), .sel(RD));
  // Probe on and_4_out
  and and_4 (and_4_out, WE, decoder_1_out3);
  register register_4 (.clock(clock), .reset(reset), .WE(and_4_out), .\input (RDVAL), .\output (register_4_output));
  // Probe on and_5_out
  and and_5 (and_5_out, WE, decoder_1_out4);
  register register_5 (.clock(clock), .reset(reset), .WE(and_5_out), .\input (RDVAL), .\output (register_5_output));
  // Probe on and_6_out
  and and_6 (and_6_out, WE, decoder_1_out5);
  // Probe on and_7_out
  register register_6 (.clock(clock), .reset(reset), .WE(and_6_out), .\input (RDVAL), .\output (register_6_output));
  // Probe on and_8_out
  and and_7 (and_7_out, WE, decoder_1_out6);
  register register_7 (.clock(clock), .reset(reset), .WE(and_7_out), .\input (RDVAL), .\output (register_7_output));
  and and_8 (and_8_out, WE, decoder_1_out7);
  register register_8 (.clock(clock), .reset(reset), .WE(and_8_out), .\input (RDVAL), .\output (register_8_output));
  assign RS2VAL = decoder_2_out3 ? register_4_output : 16'bz;  // Controlled_Buffer controlled_buffer_1
  assign RS2VAL = decoder_2_out2 ? register_3_output : 16'bz;  // Controlled_Buffer controlled_buffer_2
  assign RS2VAL = decoder_2_out1 ? register_2_output : 16'bz;  // Controlled_Buffer controlled_buffer_3
  assign RS2VAL = decoder_2_out0 ? register_1_output : 16'bz;  // Controlled_Buffer controlled_buffer_4
  Decoder #(.select(3), .enable("false")) decoder_2 (
    .out0(decoder_2_out0), .out1(decoder_2_out1), .out2(decoder_2_out2), .out3(decoder_2_out3),
    .out4(decoder_2_out4), .out5(decoder_2_out5), .out6(decoder_2_out6), .out7(decoder_2_out7), .sel(RS1));
  assign RS2VAL = decoder_2_out7 ? register_8_output : 16'bz;  // Controlled_Buffer controlled_buffer_5
  assign RS2VAL = decoder_2_out6 ? register_7_output : 16'bz;  // Controlled_Buffer controlled_buffer_6
  assign RS2VAL = decoder_2_out5 ? register_6_output : 16'bz;  // Controlled_Buffer controlled_buffer_7
  assign RS2VAL = decoder_2_out4 ? register_5_output : 16'bz;  // Controlled_Buffer controlled_buffer_8
  assign RS_nVAL = decoder_3_out3 ? register_4_output : 16'bz;  // Controlled_Buffer controlled_buffer_9
  assign RS_nVAL = decoder_3_out2 ? register_3_output : 16'bz;  // Controlled_Buffer controlled_buffer_10
  assign RS_nVAL = decoder_3_out1 ? register_2_output : 16'bz;  // Controlled_Buffer controlled_buffer_11
  assign RS_nVAL = decoder_3_out0 ? register_1_output : 16'bz;  // Controlled_Buffer controlled_buffer_12
  Decoder #(.select(3), .enable("false")) decoder_3 (
    .out0(decoder_3_out0), .out1(decoder_3_out1), .out2(decoder_3_out2), .out3(decoder_3_out3),
    .out4(decoder_3_out4), .out5(decoder_3_out5), .out6(decoder_3_out6), .out7(decoder_3_out7), .sel(RS2));
  assign RS_nVAL = decoder_3_out7 ? register_8_output : 16'bz;  // Controlled_Buffer controlled_buffer_13
  assign RS_nVAL = decoder_3_out6 ? register_7_output : 16'bz;  // Controlled_Buffer controlled_buffer_14
  assign RS_nVAL = decoder_3_out5 ? register_6_output : 16'bz;  // Controlled_Buffer controlled_buffer_15
  assign RS_nVAL = decoder_3_out4 ? register_5_output : 16'bz;  // Controlled_Buffer controlled_buffer_16
endmodule

module full_adder (
  input  A,
  input  B,
  input  Cin,
  output result,
  output Cout
);

  wire and_1_out, and_2_out, xor_1_out;

  xor xor_1 (xor_1_out, A, B);
  and and_1 (and_1_out, A, B);
  and and_2 (and_2_out, xor_1_out, Cin);
  xor xor_2 (result, xor_1_out, Cin);
  or or_1 (Cout, and_2_out, and_1_out);
endmodule

module addermain (
  input  sub,
  input  [15:0] B,
  input  [15:0] A,
  output [15:0] result,
  output ovf
);

  wire full_adder_1_cout, full_adder_2_cout, full_adder_3_cout, full_adder_4_cout, full_adder_5_cout,
       full_adder_6_cout, full_adder_7_cout, full_adder_8_cout, full_adder_9_cout, full_adder_10_cout,
       full_adder_11_cout, full_adder_12_cout, full_adder_13_cout, full_adder_14_cout, full_adder_15_cout,
       full_adder_16_cout, xor_2_out, xor_3_out, xor_4_out, xor_5_out, xor_6_out, xor_7_out, xor_8_out,
       xor_9_out, xor_10_out, xor_11_out, xor_12_out, xor_13_out, xor_14_out, xor_15_out, xor_16_out,
       xor_17_out;

  xor xor_1 (ovf, full_adder_2_cout, full_adder_1_cout);
  full_adder full_adder_1 (
    .A(A[15]), .B(xor_2_out), .Cin(full_adder_2_cout), .result(result[15]), .Cout(full_adder_1_cout));
  xor xor_2 (xor_2_out, sub, B[15]);
  full_adder full_adder_2 (
    .A(A[14]), .B(xor_4_out), .Cin(full_adder_3_cout), .result(result[14]), .Cout(full_adder_2_cout));
  full_adder full_adder_3 (
    .A(A[13]), .B(xor_3_out), .Cin(full_adder_4_cout), .result(result[13]), .Cout(full_adder_3_cout));
  xor xor_3 (xor_3_out, sub, B[13]);
  xor xor_4 (xor_4_out, sub, B[14]);
  full_adder full_adder_4 (
    .A(A[12]), .B(xor_5_out), .Cin(full_adder_5_cout), .result(result[12]), .Cout(full_adder_4_cout));
  xor xor_5 (xor_5_out, sub, B[12]);
  full_adder full_adder_5 (
    .A(A[11]), .B(xor_6_out), .Cin(full_adder_7_cout), .result(result[11]), .Cout(full_adder_5_cout));
  xor xor_6 (xor_6_out, sub, B[11]);
  full_adder full_adder_6 (
    .A(A[9]), .B(xor_8_out), .Cin(full_adder_8_cout), .result(result[9]), .Cout(full_adder_6_cout));
  full_adder full_adder_7 (
    .A(A[10]), .B(xor_7_out), .Cin(full_adder_6_cout), .result(result[10]), .Cout(full_adder_7_cout));
  xor xor_7 (xor_7_out, sub, B[10]);
  xor xor_8 (xor_8_out, sub, B[9]);
  full_adder full_adder_8 (
    .A(A[8]), .B(xor_9_out), .Cin(full_adder_9_cout), .result(result[8]), .Cout(full_adder_8_cout));
  xor xor_9 (xor_9_out, sub, B[8]);
  full_adder full_adder_9 (
    .A(A[7]), .B(xor_10_out), .Cin(full_adder_10_cout), .result(result[7]), .Cout(full_adder_9_cout));
  xor xor_10 (xor_10_out, sub, B[7]);
  full_adder full_adder_10 (
    .A(A[6]), .B(xor_11_out), .Cin(full_adder_11_cout), .result(result[6]), .Cout(full_adder_10_cout));
  full_adder full_adder_11 (
    .A(A[5]), .B(xor_12_out), .Cin(full_adder_12_cout), .result(result[5]), .Cout(full_adder_11_cout));
  xor xor_11 (xor_11_out, sub, B[6]);
  xor xor_12 (xor_12_out, sub, B[5]);
  full_adder full_adder_12 (
    .A(A[4]), .B(xor_13_out), .Cin(full_adder_13_cout), .result(result[4]), .Cout(full_adder_12_cout));
  xor xor_13 (xor_13_out, sub, B[4]);
  full_adder full_adder_13 (
    .A(A[3]), .B(xor_14_out), .Cin(full_adder_15_cout), .result(result[3]), .Cout(full_adder_13_cout));
  xor xor_14 (xor_14_out, sub, B[3]);
  full_adder full_adder_14 (
    .A(A[1]), .B(xor_15_out), .Cin(full_adder_16_cout), .result(result[1]), .Cout(full_adder_14_cout));
  full_adder full_adder_15 (
    .A(A[2]), .B(xor_16_out), .Cin(full_adder_14_cout), .result(result[2]), .Cout(full_adder_15_cout));
  xor xor_15 (xor_15_out, sub, B[1]);
  xor xor_16 (xor_16_out, sub, B[2]);
  full_adder full_adder_16 (.A(A[0]), .B(xor_17_out), .Cin(sub), .result(result[0]), .Cout(full_adder_16_cout));
  xor xor_17 (xor_17_out, sub, B[0]);
endmodule

module AND (
  input  [15:0] A,
  input  [15:0] B,
  output [15:0] result
);

  and and_1 (result[0], A[0], B[0]);
  and and_2 (result[1], A[1], B[1]);
  and and_3 (result[2], A[2], B[2]);
  and and_4 (result[3], A[3], B[3]);
  and and_5 (result[4], A[4], B[4]);
  and and_6 (result[5], A[5], B[5]);
  and and_7 (result[6], A[6], B[6]);
  and and_8 (result[7], A[7], B[7]);
  and and_9 (result[8], A[8], B[8]);
  and and_10 (result[9], A[9], B[9]);
  and and_11 (result[10], A[10], B[10]);
  and and_12 (result[11], A[11], B[11]);
  and and_13 (result[12], A[12], B[12]);
  and and_14 (result[13], A[13], B[13]);
  and and_15 (result[14], A[14], B[14]);
  and and_16 (result[15], A[15], B[15]);
endmodule

module OR (
  input  [15:0] A,
  input  [15:0] B,
  output [15:0] result
);

  or or_1 (result[0], A[0], B[0]);
  or or_2 (result[1], A[1], B[1]);
  or or_3 (result[2], A[2], B[2]);
  or or_4 (result[3], A[3], B[3]);
  or or_5 (result[4], A[4], B[4]);
  or or_6 (result[5], A[5], B[5]);
  or or_7 (result[6], A[6], B[6]);
  or or_8 (result[7], A[7], B[7]);
  or or_9 (result[8], A[8], B[8]);
  or or_10 (result[9], A[9], B[9]);
  or or_11 (result[10], A[10], B[10]);
  or or_12 (result[11], A[11], B[11]);
  or or_13 (result[12], A[12], B[12]);
  or or_14 (result[13], A[13], B[13]);
  or or_15 (result[14], A[14], B[14]);
  or or_16 (result[15], A[15], B[15]);
endmodule

module ALU_old (
  input  [15:0] A,
  input  [15:0] B,
  input  Control0,
  input  Control1,
  output [15:0] result,
  output zero,
  output Negative,
  output ovf
);

  wire or_2_out;
  wire [15:0] addermain_1_result, and_1_result, multiplexer_1_out, or_1_result;

  AND and_1 (.A(A), .B(B), .result(and_1_result));
  OR or_1 (.A(A), .B(B), .result(or_1_result));
  addermain addermain_1 (.result(addermain_1_result), .ovf(ovf), .sub(Control0), .A(A), .B(B));
  Multiplexer #(.width(16), .enable("false")) multiplexer_1 (
    .in0(and_1_result), .in1(or_1_result), .out(multiplexer_1_out), .sel(Control0));
  Multiplexer #(.width(16), .enable("false")) multiplexer_2 (
    .in0(multiplexer_1_out), .in1(addermain_1_result), .out({Negative, result[14:0]}), .sel(Control1));
  or or_2 (or_2_out, result[0], result[1], result[2], result[3], result[4], result[5], result[6], result[7], result[8], result[9], result[10], result[11], result[12], result[13], result[14], Negative);
  not not_1 (zero, or_2_out);

  assign result[15] = Negative;

  // Notes on the sheet:
  //   00 = B, 10 = A, 11 = -, 01 = +
endmodule

module ALU (
  input  sub,
  input  [15:0] InputData1,
  input  [15:0] InputData2,
  input  [2:0] OpType,
  input  [2:0] shamt,
  output [15:0] OutputData,
  output z
);

  wire or_2_out;
  wire [15:0] addermain_1_result, and_1_out, left_shifter_1_output, or_1_out, right_shifter_1_output,
       xor_1_out;

  addermain addermain_1 (.result(addermain_1_result), .sub(sub), .A(InputData1), .B(InputData2));  // open: ovf
  right_shifter right_shifter_1 (.\input (InputData1), .shamt(shamt), .\output (right_shifter_1_output));
  left_shifter left_shifter_1 (.\input (InputData1), .shamt(shamt), .\output (left_shifter_1_output));
  assign xor_1_out = InputData1 ^ InputData2;  // XOR_Gate xor_1, 16 bits wide
  assign and_1_out = InputData1 & InputData2;  // AND_Gate and_1, 16 bits wide
  assign or_1_out = InputData1 | InputData2;  // OR_Gate or_1, 16 bits wide
  Multiplexer #(.select(3), .width(16), .enable("false")) multiplexer_1 (
    .in0(addermain_1_result), .in1(xor_1_out), .in2(and_1_out), .in3(or_1_out), .in4(right_shifter_1_output),
    .in5(left_shifter_1_output), .out(OutputData), .sel(OpType));  // open: in6, in7
  or or_2 (or_2_out, OutputData[15], OutputData[14], OutputData[13], OutputData[12], OutputData[11], OutputData[10], OutputData[9], OutputData[8], OutputData[7], OutputData[6], OutputData[5], OutputData[4], OutputData[3], OutputData[2], OutputData[1], OutputData[0]);
  not not_1 (z, or_2_out);

  // Notes on the sheet:
  //   MADE INPUTDATA1 RS!!
endmodule

module _1_bit_inverter (
  input  sub,
  output result
);

  wire xor_1_out;

  full_adder full_adder_1 (.A(1'b1), .B(xor_1_out), .Cin(sub), .result(result));  // open: Cout
  xor xor_1 (xor_1_out, sub, sub);
endmodule

module ALU_old_2 (
  input  [15:0] InputData1,
  input  [15:0] InputData2,
  input  [1:0] OpType,
  output [15:0] OutputData,
  output zero,
  output Negative,
  output ovf
);

  wire n1_bit_inverter_1_result, or_2_out;
  wire [15:0] addermain_1_result, and_1_result, multiplexer_1_out, or_1_result;

  AND and_1 (.A(InputData1), .B(InputData2), .result(and_1_result));
  OR or_1 (.A(InputData1), .B(InputData2), .result(or_1_result));
  addermain addermain_1 (.result(addermain_1_result), .ovf(ovf), .sub(OpType[0]), .A(InputData1), .B(InputData2));
  Multiplexer #(.width(16), .enable("false")) multiplexer_1 (
    .in0(and_1_result), .in1(or_1_result), .out(multiplexer_1_out), .sel(OpType[0]));
  _1_bit_inverter u_1_bit_inverter_1 (.sub(OpType[1]), .result(n1_bit_inverter_1_result));
  Multiplexer #(.width(16), .enable("false")) multiplexer_2 (
    .in0(multiplexer_1_out), .in1(addermain_1_result), .out({Negative, OutputData[14:0]}),
    .sel(n1_bit_inverter_1_result));
  or or_2 (or_2_out, OutputData[0], OutputData[1], OutputData[2], OutputData[3], OutputData[4], OutputData[5], OutputData[6], OutputData[7], OutputData[8], OutputData[9], OutputData[10], OutputData[11], OutputData[12], OutputData[13], OutputData[14], Negative);
  not not_1 (zero, or_2_out);

  assign OutputData[15] = Negative;

  // Notes on the sheet:
  //   10B 11A 01SUB 00ADD
  //   00 = B, 01 = A, 11 = -, 10 = +
  //   want 00Add 01Sub 10OR 11NOT
endmodule

module right_shifter (
  input  [15:0] \input ,
  input  [2:0] shamt,
  output [15:0] \output 
);

  wire multiplexer_1_out, multiplexer_2_out, multiplexer_3_out, multiplexer_4_out, multiplexer_5_out,
       multiplexer_6_out, multiplexer_7_out, multiplexer_8_out, multiplexer_9_out, multiplexer_10_out,
       multiplexer_11_out, multiplexer_12_out, multiplexer_13_out, multiplexer_14_out, multiplexer_15_out,
       multiplexer_16_out, multiplexer_17_out, multiplexer_18_out, multiplexer_19_out, multiplexer_24_out,
       multiplexer_25_out, multiplexer_26_out, multiplexer_27_out, multiplexer_28_out, multiplexer_29_out,
       multiplexer_30_out, multiplexer_31_out, multiplexer_36_out, multiplexer_37_out, multiplexer_38_out,
       multiplexer_39_out, multiplexer_44_out;

  Multiplexer #(.enable("false")) multiplexer_1 (
    .in0(\input [0]), .in1(\input [1]), .out(multiplexer_1_out), .sel(shamt[0]));
  Multiplexer #(.enable("false")) multiplexer_2 (
    .in0(\input [1]), .in1(\input [2]), .out(multiplexer_2_out), .sel(shamt[0]));
  Multiplexer #(.enable("false")) multiplexer_3 (
    .in0(\input [2]), .in1(\input [3]), .out(multiplexer_3_out), .sel(shamt[0]));
  Multiplexer #(.enable("false")) multiplexer_4 (
    .in0(\input [3]), .in1(\input [4]), .out(multiplexer_4_out), .sel(shamt[0]));
  Multiplexer #(.enable("false")) multiplexer_5 (
    .in0(multiplexer_1_out), .in1(multiplexer_3_out), .out(multiplexer_5_out), .sel(shamt[1]));
  Multiplexer #(.enable("false")) multiplexer_6 (
    .in0(multiplexer_2_out), .in1(multiplexer_4_out), .out(multiplexer_6_out), .sel(shamt[1]));
  Multiplexer #(.enable("false")) multiplexer_7 (
    .in0(multiplexer_3_out), .in1(multiplexer_8_out), .out(multiplexer_7_out), .sel(shamt[1]));
  Multiplexer #(.enable("false")) multiplexer_8 (
    .in0(\input [4]), .in1(\input [5]), .out(multiplexer_8_out), .sel(shamt[0]));
  Multiplexer #(.enable("false")) multiplexer_9 (
    .in0(\input [5]), .in1(\input [6]), .out(multiplexer_9_out), .sel(shamt[0]));
  Multiplexer #(.enable("false")) multiplexer_10 (
    .in0(\input [6]), .in1(\input [7]), .out(multiplexer_10_out), .sel(shamt[0]));
  Multiplexer #(.enable("false")) multiplexer_11 (
    .in0(\input [7]), .in1(\input [8]), .out(multiplexer_11_out), .sel(shamt[0]));
  Multiplexer #(.enable("false")) multiplexer_12 (
    .in0(multiplexer_4_out), .in1(multiplexer_9_out), .out(multiplexer_12_out), .sel(shamt[1]));
  Multiplexer #(.enable("false")) multiplexer_13 (
    .in0(multiplexer_8_out), .in1(multiplexer_10_out), .out(multiplexer_13_out), .sel(shamt[1]));
  Multiplexer #(.enable("false")) multiplexer_14 (
    .in0(multiplexer_9_out), .in1(multiplexer_11_out), .out(multiplexer_14_out), .sel(shamt[1]));
  Multiplexer #(.enable("false")) multiplexer_15 (
    .in0(multiplexer_10_out), .in1(multiplexer_16_out), .out(multiplexer_15_out), .sel(shamt[1]));
  Multiplexer #(.enable("false")) multiplexer_16 (
    .in0(\input [8]), .in1(\input [9]), .out(multiplexer_16_out), .sel(shamt[0]));
  Multiplexer #(.enable("false")) multiplexer_17 (
    .in0(\input [9]), .in1(\input [10]), .out(multiplexer_17_out), .sel(shamt[0]));
  Multiplexer #(.enable("false")) multiplexer_18 (
    .in0(\input [10]), .in1(\input [11]), .out(multiplexer_18_out), .sel(shamt[0]));
  Multiplexer #(.enable("false")) multiplexer_19 (
    .in0(\input [11]), .in1(\input [12]), .out(multiplexer_19_out), .sel(shamt[0]));
  Multiplexer #(.enable("false")) multiplexer_20 (
    .in0(multiplexer_5_out), .in1(multiplexer_13_out), .out(\output [0]), .sel(shamt[2]));
  Multiplexer #(.enable("false")) multiplexer_21 (
    .in0(multiplexer_6_out), .in1(multiplexer_14_out), .out(\output [1]), .sel(shamt[2]));
  Multiplexer #(.enable("false")) multiplexer_22 (
    .in0(multiplexer_7_out), .in1(multiplexer_15_out), .out(\output [2]), .sel(shamt[2]));
  Multiplexer #(.enable("false")) multiplexer_23 (
    .in0(multiplexer_12_out), .in1(multiplexer_24_out), .out(\output [3]), .sel(shamt[2]));
  Multiplexer #(.enable("false")) multiplexer_24 (
    .in0(multiplexer_11_out), .in1(multiplexer_17_out), .out(multiplexer_24_out), .sel(shamt[1]));
  Multiplexer #(.enable("false")) multiplexer_25 (
    .in0(multiplexer_16_out), .in1(multiplexer_18_out), .out(multiplexer_25_out), .sel(shamt[1]));
  Multiplexer #(.enable("false")) multiplexer_26 (
    .in0(multiplexer_17_out), .in1(multiplexer_19_out), .out(multiplexer_26_out), .sel(shamt[1]));
  Multiplexer #(.enable("false")) multiplexer_27 (
    .in0(multiplexer_18_out), .in1(multiplexer_28_out), .out(multiplexer_27_out), .sel(shamt[1]));
  Multiplexer #(.enable("false")) multiplexer_28 (
    .in0(\input [12]), .in1(\input [13]), .out(multiplexer_28_out), .sel(shamt[0]));
  Multiplexer #(.enable("false")) multiplexer_29 (
    .in0(\input [13]), .in1(\input [14]), .out(multiplexer_29_out), .sel(shamt[0]));
  Multiplexer #(.enable("false")) multiplexer_30 (
    .in0(\input [14]), .in1(\input [15]), .out(multiplexer_30_out), .sel(shamt[0]));
  Multiplexer #(.enable("false")) multiplexer_31 (
    .in0(\input [15]), .in1(1'b0), .out(multiplexer_31_out), .sel(shamt[0]));
  Multiplexer #(.enable("false")) multiplexer_32 (
    .in0(multiplexer_13_out), .in1(multiplexer_25_out), .out(\output [4]), .sel(shamt[2]));
  Multiplexer #(.enable("false")) multiplexer_33 (
    .in0(multiplexer_14_out), .in1(multiplexer_26_out), .out(\output [5]), .sel(shamt[2]));
  Multiplexer #(.enable("false")) multiplexer_34 (
    .in0(multiplexer_15_out), .in1(multiplexer_27_out), .out(\output [6]), .sel(shamt[2]));
  Multiplexer #(.enable("false")) multiplexer_35 (
    .in0(multiplexer_24_out), .in1(multiplexer_36_out), .out(\output [7]), .sel(shamt[2]));
  Multiplexer #(.enable("false")) multiplexer_36 (
    .in0(multiplexer_19_out), .in1(multiplexer_29_out), .out(multiplexer_36_out), .sel(shamt[1]));
  Multiplexer #(.enable("false")) multiplexer_37 (
    .in0(multiplexer_28_out), .in1(multiplexer_30_out), .out(multiplexer_37_out), .sel(shamt[1]));
  Multiplexer #(.enable("false")) multiplexer_38 (
    .in0(multiplexer_29_out), .in1(multiplexer_31_out), .out(multiplexer_38_out), .sel(shamt[1]));
  Multiplexer #(.enable("false")) multiplexer_39 (
    .in0(multiplexer_30_out), .in1(1'b0), .out(multiplexer_39_out), .sel(shamt[1]));
  Multiplexer #(.enable("false")) multiplexer_40 (
    .in0(multiplexer_25_out), .in1(multiplexer_37_out), .out(\output [8]), .sel(shamt[2]));
  Multiplexer #(.enable("false")) multiplexer_41 (
    .in0(multiplexer_26_out), .in1(multiplexer_38_out), .out(\output [9]), .sel(shamt[2]));
  Multiplexer #(.enable("false")) multiplexer_42 (
    .in0(multiplexer_27_out), .in1(multiplexer_39_out), .out(\output [10]), .sel(shamt[2]));
  Multiplexer #(.enable("false")) multiplexer_43 (
    .in0(multiplexer_36_out), .in1(multiplexer_44_out), .out(\output [11]), .sel(shamt[2]));
  Multiplexer #(.enable("false")) multiplexer_44 (
    .in0(multiplexer_31_out), .in1(1'b0), .out(multiplexer_44_out), .sel(shamt[1]));
  Multiplexer #(.enable("false")) multiplexer_45 (
    .in0(multiplexer_37_out), .in1(1'b0), .out(\output [12]), .sel(shamt[2]));
  Multiplexer #(.enable("false")) multiplexer_46 (
    .in0(multiplexer_38_out), .in1(1'b0), .out(\output [13]), .sel(shamt[2]));
  Multiplexer #(.enable("false")) multiplexer_47 (
    .in0(multiplexer_39_out), .in1(1'b0), .out(\output [14]), .sel(shamt[2]));
  Multiplexer #(.enable("false")) multiplexer_48 (
    .in0(multiplexer_44_out), .in1(1'b0), .out(\output [15]), .sel(shamt[2]));

  // Other names for the same wires on the sheet: a = shamt[0]; b = shamt[1]; c = shamt[2]

  // Notes on the sheet:
  //   RIGHT SHIFTER
endmodule

module left_shifter (
  input  [15:0] \input ,
  input  [2:0] shamt,
  output [15:0] \output 
);

  wire multiplexer_1_out, multiplexer_2_out, multiplexer_3_out, multiplexer_4_out, multiplexer_5_out,
       multiplexer_6_out, multiplexer_7_out, multiplexer_8_out, multiplexer_9_out, multiplexer_10_out,
       multiplexer_11_out, multiplexer_12_out, multiplexer_13_out, multiplexer_14_out, multiplexer_15_out,
       multiplexer_18_out, multiplexer_19_out, multiplexer_20_out, multiplexer_21_out, multiplexer_22_out,
       multiplexer_23_out, multiplexer_24_out, multiplexer_25_out, multiplexer_30_out, multiplexer_31_out,
       multiplexer_32_out, multiplexer_33_out, multiplexer_34_out, multiplexer_35_out, multiplexer_40_out,
       multiplexer_41_out, multiplexer_42_out;

  Multiplexer #(.enable("false")) multiplexer_1 (
    .in0(\input [15]), .in1(\input [14]), .out(multiplexer_1_out), .sel(shamt[0]));
  Multiplexer #(.enable("false")) multiplexer_2 (
    .in0(\input [14]), .in1(\input [13]), .out(multiplexer_2_out), .sel(shamt[0]));
  Multiplexer #(.enable("false")) multiplexer_3 (
    .in0(multiplexer_1_out), .in1(multiplexer_4_out), .out(multiplexer_3_out), .sel(shamt[1]));
  Multiplexer #(.enable("false")) multiplexer_4 (
    .in0(\input [13]), .in1(\input [12]), .out(multiplexer_4_out), .sel(shamt[0]));
  Multiplexer #(.enable("false")) multiplexer_5 (
    .in0(\input [12]), .in1(\input [11]), .out(multiplexer_5_out), .sel(shamt[0]));
  Multiplexer #(.enable("false")) multiplexer_6 (
    .in0(\input [11]), .in1(\input [10]), .out(multiplexer_6_out), .sel(shamt[0]));
  Multiplexer #(.enable("false")) multiplexer_7 (
    .in0(\input [10]), .in1(\input [9]), .out(multiplexer_7_out), .sel(shamt[0]));
  Multiplexer #(.enable("false")) multiplexer_8 (
    .in0(multiplexer_2_out), .in1(multiplexer_5_out), .out(multiplexer_8_out), .sel(shamt[1]));
  Multiplexer #(.enable("false")) multiplexer_9 (
    .in0(multiplexer_4_out), .in1(multiplexer_6_out), .out(multiplexer_9_out), .sel(shamt[1]));
  Multiplexer #(.enable("false")) multiplexer_10 (
    .in0(multiplexer_5_out), .in1(multiplexer_7_out), .out(multiplexer_10_out), .sel(shamt[1]));
  Multiplexer #(.enable("false")) multiplexer_11 (
    .in0(multiplexer_6_out), .in1(multiplexer_12_out), .out(multiplexer_11_out), .sel(shamt[1]));
  Multiplexer #(.enable("false")) multiplexer_12 (
    .in0(\input [9]), .in1(\input [8]), .out(multiplexer_12_out), .sel(shamt[0]));
  Multiplexer #(.enable("false")) multiplexer_13 (
    .in0(\input [8]), .in1(\input [7]), .out(multiplexer_13_out), .sel(shamt[0]));
  Multiplexer #(.enable("false")) multiplexer_14 (
    .in0(\input [7]), .in1(\input [6]), .out(multiplexer_14_out), .sel(shamt[0]));
  Multiplexer #(.enable("false")) multiplexer_15 (
    .in0(\input [6]), .in1(\input [5]), .out(multiplexer_15_out), .sel(shamt[0]));
  Multiplexer #(.enable("false")) multiplexer_16 (
    .in0(multiplexer_3_out), .in1(multiplexer_11_out), .out(\output [15]), .sel(shamt[2]));
  Multiplexer #(.enable("false")) multiplexer_17 (
    .in0(multiplexer_8_out), .in1(multiplexer_18_out), .out(\output [14]), .sel(shamt[2]));
  Multiplexer #(.enable("false")) multiplexer_18 (
    .in0(multiplexer_7_out), .in1(multiplexer_13_out), .out(multiplexer_18_out), .sel(shamt[1]));
  Multiplexer #(.enable("false")) multiplexer_19 (
    .in0(multiplexer_12_out), .in1(multiplexer_14_out), .out(multiplexer_19_out), .sel(shamt[1]));
  Multiplexer #(.enable("false")) multiplexer_20 (
    .in0(multiplexer_13_out), .in1(multiplexer_15_out), .out(multiplexer_20_out), .sel(shamt[1]));
  Multiplexer #(.enable("false")) multiplexer_21 (
    .in0(multiplexer_14_out), .in1(multiplexer_22_out), .out(multiplexer_21_out), .sel(shamt[1]));
  Multiplexer #(.enable("false")) multiplexer_22 (
    .in0(\input [5]), .in1(\input [4]), .out(multiplexer_22_out), .sel(shamt[0]));
  Multiplexer #(.enable("false")) multiplexer_23 (
    .in0(\input [4]), .in1(\input [3]), .out(multiplexer_23_out), .sel(shamt[0]));
  Multiplexer #(.enable("false")) multiplexer_24 (
    .in0(\input [3]), .in1(\input [2]), .out(multiplexer_24_out), .sel(shamt[0]));
  Multiplexer #(.enable("false")) multiplexer_25 (
    .in0(\input [2]), .in1(\input [1]), .out(multiplexer_25_out), .sel(shamt[0]));
  Multiplexer #(.enable("false")) multiplexer_26 (
    .in0(multiplexer_9_out), .in1(multiplexer_19_out), .out(\output [13]), .sel(shamt[2]));
  Multiplexer #(.enable("false")) multiplexer_27 (
    .in0(multiplexer_10_out), .in1(multiplexer_20_out), .out(\output [12]), .sel(shamt[2]));
  Multiplexer #(.enable("false")) multiplexer_28 (
    .in0(multiplexer_11_out), .in1(multiplexer_21_out), .out(\output [11]), .sel(shamt[2]));
  Multiplexer #(.enable("false")) multiplexer_29 (
    .in0(multiplexer_18_out), .in1(multiplexer_30_out), .out(\output [10]), .sel(shamt[2]));
  Multiplexer #(.enable("false")) multiplexer_30 (
    .in0(multiplexer_15_out), .in1(multiplexer_23_out), .out(multiplexer_30_out), .sel(shamt[1]));
  Multiplexer #(.enable("false")) multiplexer_31 (
    .in0(multiplexer_22_out), .in1(multiplexer_24_out), .out(multiplexer_31_out), .sel(shamt[1]));
  Multiplexer #(.enable("false")) multiplexer_32 (
    .in0(multiplexer_23_out), .in1(multiplexer_25_out), .out(multiplexer_32_out), .sel(shamt[1]));
  Multiplexer #(.enable("false")) multiplexer_33 (
    .in0(multiplexer_24_out), .in1(multiplexer_34_out), .out(multiplexer_33_out), .sel(shamt[1]));
  Multiplexer #(.enable("false")) multiplexer_34 (
    .in0(\input [1]), .in1(\input [0]), .out(multiplexer_34_out), .sel(shamt[0]));
  Multiplexer #(.enable("false")) multiplexer_35 (
    .in0(\input [0]), .in1(1'b0), .out(multiplexer_35_out), .sel(shamt[0]));
  Multiplexer #(.enable("false")) multiplexer_36 (
    .in0(multiplexer_19_out), .in1(multiplexer_31_out), .out(\output [9]), .sel(shamt[2]));
  Multiplexer #(.enable("false")) multiplexer_37 (
    .in0(multiplexer_20_out), .in1(multiplexer_32_out), .out(\output [8]), .sel(shamt[2]));
  Multiplexer #(.enable("false")) multiplexer_38 (
    .in0(multiplexer_21_out), .in1(multiplexer_33_out), .out(\output [7]), .sel(shamt[2]));
  Multiplexer #(.enable("false")) multiplexer_39 (
    .in0(multiplexer_30_out), .in1(multiplexer_40_out), .out(\output [6]), .sel(shamt[2]));
  Multiplexer #(.enable("false")) multiplexer_40 (
    .in0(multiplexer_25_out), .in1(multiplexer_35_out), .out(multiplexer_40_out), .sel(shamt[1]));
  Multiplexer #(.enable("false")) multiplexer_41 (
    .in0(multiplexer_34_out), .in1(1'b0), .out(multiplexer_41_out), .sel(shamt[1]));
  Multiplexer #(.enable("false")) multiplexer_42 (
    .in0(multiplexer_35_out), .in1(1'b0), .out(multiplexer_42_out), .sel(shamt[1]));
  Multiplexer #(.enable("false")) multiplexer_43 (
    .in0(multiplexer_31_out), .in1(multiplexer_41_out), .out(\output [5]), .sel(shamt[2]));
  Multiplexer #(.enable("false")) multiplexer_44 (
    .in0(multiplexer_32_out), .in1(multiplexer_42_out), .out(\output [4]), .sel(shamt[2]));
  Multiplexer #(.enable("false")) multiplexer_45 (
    .in0(multiplexer_33_out), .in1(1'b0), .out(\output [3]), .sel(shamt[2]));
  Multiplexer #(.enable("false")) multiplexer_46 (
    .in0(multiplexer_40_out), .in1(1'b0), .out(\output [2]), .sel(shamt[2]));
  Multiplexer #(.enable("false")) multiplexer_47 (
    .in0(multiplexer_41_out), .in1(1'b0), .out(\output [1]), .sel(shamt[2]));
  Multiplexer #(.enable("false")) multiplexer_48 (
    .in0(multiplexer_42_out), .in1(1'b0), .out(\output [0]), .sel(shamt[2]));

  // Other names for the same wires on the sheet: a = shamt[0]; b = shamt[1]; c = shamt[2]

  // Notes on the sheet:
  //   LEFT SHIFTER
endmodule

module control (
  input  [3:0] opcode,
  output BR,
  output JP,
  output DMwe,
  output Rwe
);

  wire demultiplexer_1_out0, demultiplexer_1_out1, demultiplexer_1_out2, demultiplexer_1_out3,
       demultiplexer_1_out4, demultiplexer_1_out5, demultiplexer_1_out6, demultiplexer_1_out7,
       demultiplexer_1_out8, demultiplexer_1_out9, demultiplexer_1_out10, demultiplexer_1_out11,
       demultiplexer_1_out12;

  Demultiplexer #(.select(4), .enable("false")) demultiplexer_1 (
    .out0(demultiplexer_1_out0), .out1(demultiplexer_1_out1), .out2(demultiplexer_1_out2),
    .out3(demultiplexer_1_out3), .out4(demultiplexer_1_out4), .out5(demultiplexer_1_out5),
    .out6(demultiplexer_1_out6), .out7(demultiplexer_1_out7), .out8(demultiplexer_1_out8),
    .out9(demultiplexer_1_out9), .out10(demultiplexer_1_out10), .out11(demultiplexer_1_out11),
    .out12(demultiplexer_1_out12), .out13(DMwe), .out14(BR), .out15(JP), .in(1'b1), .sel(opcode));
endmodule

module decoder (
  input  [3:0] in_1
);

  wire add, addi, blt, bne, \input , IType, j, jal, jr, JType, lw, \not , \output , RType, sll, srl, sub, sw,
       WE, \xor ;

  and and_1 (add, ~in_1[3], ~in_1[2], ~in_1[1], ~in_1[0]);  // AND_Gate
  and and_2 (addi, ~in_1[3], ~in_1[2], ~in_1[1], in_1[0]);  // AND_Gate
  and and_3 (sub, ~in_1[3], ~in_1[2], in_1[1], ~in_1[0]);  // AND_Gate
  and and_4 (\not , ~in_1[3], ~in_1[2], in_1[1], in_1[0]);  // AND_Gate
  and and_5 (\xor , ~in_1[3], in_1[2], ~in_1[1], ~in_1[0]);  // AND_Gate
  and and_6 (sll, ~in_1[3], in_1[2], ~in_1[1], in_1[0]);  // AND_Gate
  and and_7 (srl, ~in_1[3], in_1[2], in_1[1], ~in_1[0]);  // AND_Gate
  and and_8 (lw, ~in_1[3], in_1[2], in_1[1], in_1[0]);  // AND_Gate
  and and_9 (sw, in_1[3], ~in_1[2], ~in_1[1], ~in_1[0]);  // AND_Gate
  and and_10 (bne, in_1[3], ~in_1[2], ~in_1[1], in_1[0]);  // AND_Gate
  and and_11 (blt, in_1[3], ~in_1[2], in_1[1], ~in_1[0]);  // AND_Gate
  and and_12 (j, in_1[3], ~in_1[2], in_1[1], in_1[0]);  // AND_Gate
  and and_13 (jr, in_1[3], in_1[2], ~in_1[1], ~in_1[0]);  // AND_Gate
  and and_14 (jal, in_1[3], in_1[2], ~in_1[1], in_1[0]);  // AND_Gate
  and and_15 (\input , in_1[3], in_1[2], in_1[1], ~in_1[0]);  // AND_Gate
  and and_16 (\output , in_1[3], in_1[2], in_1[1], in_1[0]);
  or or_1 (WE, srl, add, \xor , sub, \input , \not , sll, jal, addi, lw);
  or or_2 (JType, \input , addi, lw, sw, bne, blt, \output );
  or or_3 (RType, srl, sll, \xor , \not , sub, add, jr);
  or or_4 (IType, j, jal);

  // Other names for the same wires on the sheet: _4 = in_1[0]; _3 = in_1[1]; _2 = in_1[2]; _1 = in_1[3]
endmodule
